// Logisim project counter.circ as structural Verilog: 4 circuits, main circuit main
module main (
  input  clock,
  output x3,
  output x2,
  output x1,
  output x0
);

  wire and_1_out, and_2_out, and_3_out, not_1_out, or_1_out, or_2_out, ttrigger_1_nq, ttrigger_2_nq,
       ttrigger_3_nq;

  and and_1 (and_1_out, clock, or_2_out);
  not not_1 (not_1_out, clock);
  and and_2 (and_2_out, not_1_out, or_2_out);
  Ttrigger ttrigger_1 (.T(and_2_out), .C(and_2_out), .Q(x0), .nQ(ttrigger_1_nq));
  or or_1 (or_1_out, not_1_out, or_2_out);
  Ttrigger ttrigger_2 (.T(ttrigger_1_nq), .C(ttrigger_1_nq), .Q(x1), .nQ(ttrigger_2_nq));
  and and_3 (and_3_out, ttrigger_2_nq, or_1_out);
  Ttrigger ttrigger_3 (.T(and_3_out), .C(and_3_out), .Q(x2), .nQ(ttrigger_3_nq));
  Ttrigger ttrigger_4 (.T(ttrigger_3_nq), .C(ttrigger_3_nq), .Q(x3));  // open: nQ
  or or_2 (or_2_out, x3, x2, and_1_out, x1, x0);
endmodule

module RSTrigger (
  input  S,
  input  C,
  input  R,
  output Q,
  output nQ
);

  wire and_1_out, and_2_out, nor_2_out, por_1_out;

  and and_1 (and_1_out, R, C);
  and and_2 (and_2_out, C, S);
  POR por_1 (.out(por_1_out));
  nor nor_1 (Q, and_1_out, nQ);
  nor nor_2 (nor_2_out, Q, and_2_out);
  or or_1 (nQ, nor_2_out, por_1_out);
endmodule

module JK (
  input  J,
  input  C,
  input  K,
  output Q,
  output nQ
);

  wire and_1_out, and_2_out, not_1_out, rstrigger_1_nq, rstrigger_1_q;

  and and_1 (and_1_out, nQ, J);
  and and_2 (and_2_out, K, Q);
  not not_1 (not_1_out, C);
  RSTrigger rstrigger_1 (.S(and_1_out), .C(C), .R(and_2_out), .Q(rstrigger_1_q), .nQ(rstrigger_1_nq));
  RSTrigger rstrigger_2 (.S(rstrigger_1_q), .C(not_1_out), .R(rstrigger_1_nq), .Q(Q), .nQ(nQ));
endmodule

module Ttrigger (
  input  T,
  input  C,
  output Q,
  output nQ
);

  JK jk_1 (.J(T), .C(C), .K(T), .Q(Q), .nQ(nQ));
endmodule
