// Logisim project lfsr.circ as structural Verilog: 4 circuits, main circuit main
module main (
  input  clock,
  input  x7,
  input  x6,
  input  x5,
  input  x4,
  input  x3,
  input  x2,
  input  x1,
  input  x0,
  output Q,
  output y7,
  output y6,
  output y5,
  output y4,
  output y3,
  output y2,
  output y1,
  output y0
);

  wire not_1_out;

  not not_1 (not_1_out, clock);
  modJK modjk_1 (.T(Q), .S(x7), .C(not_1_out), .Q(y7));  // open: nQ
  modJK modjk_2 (.T(y7), .S(x6), .C(not_1_out), .Q(y6));  // open: nQ
  modJK modjk_3 (.T(y6), .S(x5), .C(not_1_out), .Q(y5));  // open: nQ
  modJK modjk_4 (.T(y5), .S(x4), .C(not_1_out), .Q(y4));  // open: nQ
  modJK modjk_5 (.T(y4), .S(x3), .C(not_1_out), .Q(y3));  // open: nQ
  modJK modjk_6 (.T(y3), .S(x2), .C(not_1_out), .Q(y2));  // open: nQ
  modJK modjk_7 (.T(y2), .S(x1), .C(not_1_out), .Q(y1));  // open: nQ
  modJK modjk_8 (.T(y1), .S(x0), .C(not_1_out), .Q(y0));  // open: nQ
  ExactlyOne xor_1 (.out(Q), .in0(y7), .in1(y1), .in2(y0));
endmodule

module RSTrigger (
  input  S,
  input  C,
  input  R,
  output Q,
  output nQ
);

  wire and_1_out, and_2_out, nor_2_out, por_1_out;

  and and_1 (and_1_out, R, C);
  and and_2 (and_2_out, C, S);
  POR por_1 (.out(por_1_out));
  nor nor_1 (Q, and_1_out, nQ);
  nor nor_2 (nor_2_out, Q, and_2_out);
  or or_1 (nQ, nor_2_out, por_1_out);
endmodule

module JK (
  input  J,
  input  C,
  input  K,
  output Q,
  output nQ
);

  wire and_1_out, and_2_out, not_1_out, rstrigger_1_nq, rstrigger_1_q;

  and and_1 (and_1_out, nQ, J);
  and and_2 (and_2_out, K, Q);
  not not_1 (not_1_out, C);
  RSTrigger rstrigger_1 (.S(and_1_out), .C(C), .R(and_2_out), .Q(rstrigger_1_q), .nQ(rstrigger_1_nq));
  RSTrigger rstrigger_2 (.S(rstrigger_1_q), .C(not_1_out), .R(rstrigger_1_nq), .Q(Q), .nQ(nQ));
endmodule

module modJK (
  input  T,
  input  S,
  input  C,
  output Q,
  output nQ
);

  wire not_1_out, or_1_out;

  or or_1 (or_1_out, T, S);
  JK jk_1 (.J(or_1_out), .C(C), .K(not_1_out), .Q(Q), .nQ(nQ));
  not not_1 (not_1_out, or_1_out);
endmodule
